# Fritzing sketch schematic (saved by Fritzing 0.9.3b)
breadboards: 1

parts:
  U1 = OV7670 Camera [package=camera_sfv24r-2st_2]
  Part1 = Arduino Nano 33 BLE Sense
  LCD1 = TFT 1.8 inch 160x128 w SD

nets:
  3V3: U1.3V3, Part1.3V3, LCD1.pin_8
  N1: U1.SIOC, Part1.A5
  N2: U1.VSYNC, Part1.D8
  N3: U1.PCLK, Part1.A0
  N4: U1.D7, U1.D5, Part1.D4, Part1.D5~
  N5: U1.D3, Part1.D2
  N6: U1.D1, Part1.TX
  GND: U1.GND, Part1.GND, Part1.A7, LCD1.pin2, LCD1.pin3
  N7: U1.SIDO, Part1.A4
  N8: U1.HREF, Part1.A1
  N9: U1.XCLK, Part1.D9~
  N10: U1.D6, U1.D4, Part1.D3~, Part1.D6~
  N11: U1.D2, Part1.RX
  N12: U1.D0, Part1.D10~
  N13: Part1.D7, LCD1.pin4
  N14: Part1.D11/MOSI, Part1.+5V, LCD1.pin_1, LCD1.pin_6
  N15: Part1.A6, LCD1.pin_5

custom parts:
  OV7670 Camera: CMOS image sensor
  Arduino Nano 33 BLE Sense: The Nano 33 BLE Sense (without headers) is Arduino’s 3.3V AI enabled board in the smallest available form factor: 45x18mm! The Arduino Nano 33 BLE Sense is a completely new board on a well-known form factor. It comes with a series of embedded sensors: 9 axis inertial sensor: what makes this board ideal for wearable devices humidity, and temperature sensor: to get highly accurate measurements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
  TFT 1.8 inch 160x128 w SD: This is a generic 1.8 tft spi lcd display available on ebay and others. The 1.8" display has 128x160 color pixels and in this version pin names in breadboard (unlike the real board).
